// Logisim project tictactoe.circ as structural Verilog: 5 circuits, main circuit main
module main (
);

  wire and_2_out, and_3_out, button_1_out, button_2_out, button_3_out, button_4_out, button_5_out,
       button_6_out, button_7_out, button_8_out, button_9_out, cdm_8_mark5_1_p4, cdm_8_mark5_1_p5,
       cdm_8_mark5_1_p7, cdm_8_mark5_1_p8, cdm_8_mark5_1_p9, cdm_8_mark5_1_p10, cdm_8_mark5_1_p11,
       cdm_8_mark5_1_p12, cdm_8_mark5_1_p13, clk, decoder_1_out0, decoder_1_out1, decoder_2_out0,
       decoder_2_out1, game_state_display_driver_1_draw, game_state_display_driver_1_lose,
       game_state_display_driver_1_win, IAck, In_out_prime, IOsel, IRQ, not_1_out, not_2_out;
  wire [1:0] symbol_display_router_1_h0, symbol_display_router_1_h1, symbol_display_router_1_h2,
       symbol_display_router_1_v0, symbol_display_router_1_v1, symbol_display_router_1_v2;
  wire [2:0] vec;
  wire [2:2] tic_tac_toe_cell_1_hout, tic_tac_toe_cell_1_vout, tic_tac_toe_cell_2_hout,
       tic_tac_toe_cell_3_hout, tic_tac_toe_cell_4_vout, tic_tac_toe_cell_7_vout;
  wire [3:0] button_press_capture_1_xy, IOadr, tic_tac_toe_cell_1_l0, tic_tac_toe_cell_1_l1,
       tic_tac_toe_cell_1_l2, tic_tac_toe_cell_1_l3, tic_tac_toe_cell_2_l0, tic_tac_toe_cell_2_l1,
       tic_tac_toe_cell_2_l2, tic_tac_toe_cell_2_l3, tic_tac_toe_cell_3_l0, tic_tac_toe_cell_3_l1,
       tic_tac_toe_cell_3_l2, tic_tac_toe_cell_3_l3, tic_tac_toe_cell_4_l0, tic_tac_toe_cell_4_l1,
       tic_tac_toe_cell_4_l2, tic_tac_toe_cell_4_l3, tic_tac_toe_cell_5_l0, tic_tac_toe_cell_5_l1,
       tic_tac_toe_cell_5_l2, tic_tac_toe_cell_5_l3, tic_tac_toe_cell_6_l0, tic_tac_toe_cell_6_l1,
       tic_tac_toe_cell_6_l2, tic_tac_toe_cell_6_l3, tic_tac_toe_cell_7_l0, tic_tac_toe_cell_7_l1,
       tic_tac_toe_cell_7_l2, tic_tac_toe_cell_7_l3, tic_tac_toe_cell_8_l0, tic_tac_toe_cell_8_l1,
       tic_tac_toe_cell_8_l2, tic_tac_toe_cell_8_l3, tic_tac_toe_cell_9_l0, tic_tac_toe_cell_9_l1,
       tic_tac_toe_cell_9_l2, tic_tac_toe_cell_9_l3;
  wire [7:0] cdm_8_mark5_1_p16, cdm_8_mark5_1_p17, IOdat;
  wire [7:4] cdm_8_mark5_1_p15;
  wire [7:7] button_press_capture_1_ready;

  Clock clock_1 (.out(clk));
  // Probe on cdm_8_mark5_1_p5
  // Probe on cdm_8_mark5_1_p4
  LED led_1 (.in(game_state_display_driver_1_draw));
  LED led_2 (.in(game_state_display_driver_1_lose));
  LED led_3 (.in(game_state_display_driver_1_win));
  Game_State_Display_Driver game_state_display_driver_1 (
    .score(IOdat[7:6]), .clock(decoder_2_out0), .win(game_state_display_driver_1_win),
    .lose(game_state_display_driver_1_lose), .draw(game_state_display_driver_1_draw));
  // Probe on cdm_8_mark5_1_p8
  // Probe on cdm_8_mark5_1_p7
  // Probe on cdm_8_mark5_1_p10
  // Probe on cdm_8_mark5_1_p9
  Symbol_Display_Router symbol_display_router_1 (
    .clock(decoder_2_out0), .XY(IOdat[5:2]), .SymID(IOdat[1:0]), .H0(symbol_display_router_1_h0),
    .H1(symbol_display_router_1_h1), .H2(symbol_display_router_1_h2), .V0(symbol_display_router_1_v0),
    .V1(symbol_display_router_1_v1), .V2(symbol_display_router_1_v2));
  and and_1 (IOsel, IOadr[0], IOadr[1], ~IOadr[2], ~IOadr[3], cdm_8_mark5_1_p15[4], cdm_8_mark5_1_p15[5], cdm_8_mark5_1_p15[6], cdm_8_mark5_1_p15[7], decoder_1_out1);  // AND_Gate
  // Probe on cdm_8_mark5_1_p11
  Decoder #(.disabled(0)) decoder_1 (
    .out0(decoder_1_out0), .out1(decoder_1_out1), .sel(cdm_8_mark5_1_p12), .en(cdm_8_mark5_1_p13));
  // CdM_8_mark5 cdm_8_mark5_1: pin names not known; wires that end beside it: IRQ, vec, IAck, cdm_8_mark5_1_p4, cdm_8_mark5_1_p5, clk, cdm_8_mark5_1_p7, cdm_8_mark5_1_p8, cdm_8_mark5_1_p9, cdm_8_mark5_1_p10, cdm_8_mark5_1_p11, cdm_8_mark5_1_p12, cdm_8_mark5_1_p13, In_out_prime, {cdm_8_mark5_1_p15, IOadr}, cdm_8_mark5_1_p16, cdm_8_mark5_1_p17
  not not_1 (not_1_out, In_out_prime);
  assign IOdat = not_1_out ? cdm_8_mark5_1_p16 : 8'bz;  // Controlled_Buffer controlled_buffer_1
  assign cdm_8_mark5_1_p17 = In_out_prime ? IOdat : 8'bz;  // Controlled_Buffer controlled_buffer_2
  Tic_Tac_Toe_Cell tic_tac_toe_cell_1 (
    .hin(symbol_display_router_1_h0), .vin(symbol_display_router_1_v0), .button(button_1_out),
    .hout(tic_tac_toe_cell_1_hout[2]), .L0(tic_tac_toe_cell_1_l0), .L1(tic_tac_toe_cell_1_l1),
    .L2(tic_tac_toe_cell_1_l2), .L3(tic_tac_toe_cell_1_l3), .vout(tic_tac_toe_cell_1_vout[2]));
  DotMatrix #(.inputtype("row"), .matrixcols(4), .matrixrows(4)) dotmatrix_1 (
    .row0(tic_tac_toe_cell_1_l0), .row1(tic_tac_toe_cell_1_l1), .row2(tic_tac_toe_cell_1_l2),
    .row3(tic_tac_toe_cell_1_l3));
  Tic_Tac_Toe_Cell tic_tac_toe_cell_2 (
    .hin(symbol_display_router_1_h1), .vin(symbol_display_router_1_v0), .button(button_2_out),
    .hout(tic_tac_toe_cell_2_hout[2]), .L0(tic_tac_toe_cell_2_l0), .L1(tic_tac_toe_cell_2_l1),
    .L2(tic_tac_toe_cell_2_l2), .L3(tic_tac_toe_cell_2_l3), .vout(tic_tac_toe_cell_1_vout[2]));
  DotMatrix #(.inputtype("row"), .matrixcols(4), .matrixrows(4)) dotmatrix_2 (
    .row0(tic_tac_toe_cell_2_l0), .row1(tic_tac_toe_cell_2_l1), .row2(tic_tac_toe_cell_2_l2),
    .row3(tic_tac_toe_cell_2_l3));
  Tic_Tac_Toe_Cell tic_tac_toe_cell_3 (
    .hin(symbol_display_router_1_h2), .vin(symbol_display_router_1_v0), .button(button_3_out),
    .hout(tic_tac_toe_cell_3_hout[2]), .L0(tic_tac_toe_cell_3_l0), .L1(tic_tac_toe_cell_3_l1),
    .L2(tic_tac_toe_cell_3_l2), .L3(tic_tac_toe_cell_3_l3), .vout(tic_tac_toe_cell_1_vout[2]));
  DotMatrix #(.inputtype("row"), .matrixcols(4), .matrixrows(4)) dotmatrix_3 (
    .row0(tic_tac_toe_cell_3_l0), .row1(tic_tac_toe_cell_3_l1), .row2(tic_tac_toe_cell_3_l2),
    .row3(tic_tac_toe_cell_3_l3));
  and and_2 (and_2_out, decoder_1_out1, ~IOsel);  // AND_Gate
  Decoder #(.disabled(0)) decoder_2 (.out0(decoder_2_out0), .out1(decoder_2_out1), .sel(In_out_prime), .en(and_3_out));
  and and_3 (and_3_out, IOsel, IOadr[0], IOadr[1], ~IOadr[2], ~IOadr[3]);  // AND_Gate
  Button button_1 (.out(button_1_out));
  Button button_2 (.out(button_2_out));
  Button button_3 (.out(button_3_out));
  // Probe on {cdm_8_mark5_1_p15, IOadr}
  Tic_Tac_Toe_Cell tic_tac_toe_cell_4 (
    .hin(symbol_display_router_1_h0), .vin(symbol_display_router_1_v1), .button(button_4_out),
    .hout(tic_tac_toe_cell_1_hout[2]), .L0(tic_tac_toe_cell_4_l0), .L1(tic_tac_toe_cell_4_l1),
    .L2(tic_tac_toe_cell_4_l2), .L3(tic_tac_toe_cell_4_l3), .vout(tic_tac_toe_cell_4_vout[2]));
  DotMatrix #(.inputtype("row"), .matrixcols(4), .matrixrows(4)) dotmatrix_4 (
    .row0(tic_tac_toe_cell_4_l0), .row1(tic_tac_toe_cell_4_l1), .row2(tic_tac_toe_cell_4_l2),
    .row3(tic_tac_toe_cell_4_l3));
  Button button_4 (.out(button_4_out));
  Tic_Tac_Toe_Cell tic_tac_toe_cell_5 (
    .hin(symbol_display_router_1_h1), .vin(symbol_display_router_1_v1), .button(button_5_out),
    .hout(tic_tac_toe_cell_2_hout[2]), .L0(tic_tac_toe_cell_5_l0), .L1(tic_tac_toe_cell_5_l1),
    .L2(tic_tac_toe_cell_5_l2), .L3(tic_tac_toe_cell_5_l3), .vout(tic_tac_toe_cell_4_vout[2]));
  DotMatrix #(.inputtype("row"), .matrixcols(4), .matrixrows(4)) dotmatrix_5 (
    .row0(tic_tac_toe_cell_5_l0), .row1(tic_tac_toe_cell_5_l1), .row2(tic_tac_toe_cell_5_l2),
    .row3(tic_tac_toe_cell_5_l3));
  Button button_5 (.out(button_5_out));
  Tic_Tac_Toe_Cell tic_tac_toe_cell_6 (
    .hin(symbol_display_router_1_h2), .vin(symbol_display_router_1_v1), .button(button_6_out),
    .hout(tic_tac_toe_cell_3_hout[2]), .L0(tic_tac_toe_cell_6_l0), .L1(tic_tac_toe_cell_6_l1),
    .L2(tic_tac_toe_cell_6_l2), .L3(tic_tac_toe_cell_6_l3), .vout(tic_tac_toe_cell_4_vout[2]));
  DotMatrix #(.inputtype("row"), .matrixcols(4), .matrixrows(4)) dotmatrix_6 (
    .row0(tic_tac_toe_cell_6_l0), .row1(tic_tac_toe_cell_6_l1), .row2(tic_tac_toe_cell_6_l2),
    .row3(tic_tac_toe_cell_6_l3));
  Button button_6 (.out(button_6_out));
  not not_2 (not_2_out, clk);
  DotMatrix #(.inputtype("row"), .matrixcols(4), .matrixrows(4)) dotmatrix_7 (
    .row0(tic_tac_toe_cell_7_l0), .row1(tic_tac_toe_cell_7_l1), .row2(tic_tac_toe_cell_7_l2),
    .row3(tic_tac_toe_cell_7_l3));
  Tic_Tac_Toe_Cell tic_tac_toe_cell_7 (
    .hin(symbol_display_router_1_h0), .vin(symbol_display_router_1_v2), .button(button_7_out),
    .hout(tic_tac_toe_cell_1_hout[2]), .L0(tic_tac_toe_cell_7_l0), .L1(tic_tac_toe_cell_7_l1),
    .L2(tic_tac_toe_cell_7_l2), .L3(tic_tac_toe_cell_7_l3), .vout(tic_tac_toe_cell_7_vout[2]));
  Button button_7 (.out(button_7_out));
  Tic_Tac_Toe_Cell tic_tac_toe_cell_8 (
    .hin(symbol_display_router_1_h1), .vin(symbol_display_router_1_v2), .button(button_8_out),
    .hout(tic_tac_toe_cell_2_hout[2]), .L0(tic_tac_toe_cell_8_l0), .L1(tic_tac_toe_cell_8_l1),
    .L2(tic_tac_toe_cell_8_l2), .L3(tic_tac_toe_cell_8_l3), .vout(tic_tac_toe_cell_7_vout[2]));
  DotMatrix #(.inputtype("row"), .matrixcols(4), .matrixrows(4)) dotmatrix_8 (
    .row0(tic_tac_toe_cell_8_l0), .row1(tic_tac_toe_cell_8_l1), .row2(tic_tac_toe_cell_8_l2),
    .row3(tic_tac_toe_cell_8_l3));
  Button button_8 (.out(button_8_out));
  Tic_Tac_Toe_Cell tic_tac_toe_cell_9 (
    .hin(symbol_display_router_1_h2), .vin(symbol_display_router_1_v2), .button(button_9_out),
    .hout(tic_tac_toe_cell_3_hout[2]), .L0(tic_tac_toe_cell_9_l0), .L1(tic_tac_toe_cell_9_l1),
    .L2(tic_tac_toe_cell_9_l2), .L3(tic_tac_toe_cell_9_l3), .vout(tic_tac_toe_cell_7_vout[2]));
  DotMatrix #(.inputtype("row"), .matrixcols(4), .matrixrows(4)) dotmatrix_9 (
    .row0(tic_tac_toe_cell_9_l0), .row1(tic_tac_toe_cell_9_l1), .row2(tic_tac_toe_cell_9_l2),
    .row3(tic_tac_toe_cell_9_l3));
  Button button_9 (.out(button_9_out));
  // Probe on IOdat
  RAM ram_1 (
    .addr({cdm_8_mark5_1_p15, IOadr}), .data(IOdat), .sel(and_2_out), .clk(not_2_out), .ld(In_out_prime));  // open: clr
  ROM rom_1 (.addr({cdm_8_mark5_1_p15, IOadr}), .data(IOdat), .sel(decoder_1_out0));
  assign IOdat = decoder_2_out1 ? {button_press_capture_1_ready[7], 3'b000, button_press_capture_1_xy} : 8'bz;  // Controlled_Buffer controlled_buffer_3
  Button_Press_Capture button_press_capture_1 (
    .H2(tic_tac_toe_cell_3_hout[2]), .XY(button_press_capture_1_xy), .H1(tic_tac_toe_cell_2_hout[2]),
    .H0(tic_tac_toe_cell_1_hout[2]), .V2(tic_tac_toe_cell_7_vout[2]), .V1(tic_tac_toe_cell_4_vout[2]),
    .V0(tic_tac_toe_cell_1_vout[2]), .reset(decoder_2_out1), .ready(button_press_capture_1_ready[7]));

  // Other names for the same wires on the sheet: READwrite = In_out_prime

  // Notes on the sheet:
  //   lose | draw | win
  //   contents of rom_1 (hex, n*v repeats v):
  //   0 1 2 4 5 6 8 9 a 0 4 8 1 5 9 2 6 a 0 5 a 8 5 2 0 1 2 0 40 80 c0 d0 f0 c1 d1 27 a4 c5 cd 0 d6 3d bd
  //   5 e0 30 ee 28 d6 9d a e0 37 ee 3c d6 b8 a e0 28 d4 d0 f3 b3 f e0 3f d0 f 43 d7 c1 c3 d0 0 d3 9 8b e0
  //   71 f2 8c ba a e1 5a 8c 8c ee 4d f1 8c b5 76 e0 64 3a 8c ee 4d f1 8c b5 76 e0 6d 3a ee 4d ee 71 ee 4d
  //   a e1 88 d3 a d0 0 d2 3 8b e0 88 f1 8c b5 5 e1 86 3a ee 88 ee 7a c7 c5 d7 f 2f 2f 6*2a 57 5b d0 f3 a3
  //   d0 c a2 d7 d1 19 f5 ad d6 47 d6 8b d7 d0 0 d2 a 8a e0 b7 f3 bd 5 e1 b4 ee b7 8c ee aa d7 d6 a6 d1 1a
  //   f5 ad d6 47 d6 8b d7
endmodule

module Tic_Tac_Toe_Cell (
  input  [1:0] hin,
  input  [1:0] vin,
  input  button,
  output [3:0] L0,
  output [3:0] L1,
  output [3:0] L2,
  output [3:0] L3,
  output hout,
  output vout
);

  wire and_1_out;
  wire [1:0] sym_req_q;

  Pull_Resistor pull_resistor_1 (.node(hin[1]));
  Pull_Resistor pull_resistor_2 (.node(vin[1]));
  Transistor #(.\type ("n")) transistor_1 (.in(1'b0), .out(hout), .gate(button));
  and and_1 (and_1_out, hin[1], vin[1]);
  Register #(.width(2), .trigger("high")) sym_req (
    .D({vin[0], hin[0]}), .en(and_1_out), .Q(sym_req_q), .clk(and_1_out));  // open: clr
  ROM #(.addrWidth(2), .dataWidth(16)) rom_1 (.addr(sym_req_q), .data({L3, L2, L1, L0}));  // open: sel

  assign vout = hout;

  // Notes on the sheet:
  //   symID
  //   addr
  //   symbols
  //   bitmap
  //   contents of rom_1 (hex, n*v repeats v):
  //   0 9429 f99f 1234
endmodule

module Button_Press_Capture (
  input  reset,
  input  H0,
  input  H1,
  input  H2,
  input  V0,
  input  V1,
  input  V2,
  output ready,
  output [3:0] XY
);

  wire and_1_out, and_2_out, and_3_out, buffer_1_out, buffer_4_out, not_1_out, not_2_out, not_3_out,
       not_4_out, not_5_out, not_6_out, not_7_out;
  wire [1:0] multiplexer_1_out, multiplexer_4_out;

  Multiplexer #(.width(2), .enable("false")) multiplexer_1 (
    .in0(2'b00), .out(multiplexer_1_out), .sel(H0));  // open: in1
  buf buffer_1 (buffer_1_out, H0);
  Multiplexer #(.width(2), .enable("false")) multiplexer_2 (
    .in0(2'b01), .out(multiplexer_1_out), .sel(H1));  // open: in1
  Pull_Resistor #(.pull(1)) pull_resistor_1 (.node(buffer_1_out));
  buf buffer_2 (buffer_1_out, H1);
  Multiplexer #(.width(2), .enable("false")) multiplexer_3 (
    .in0(2'b10), .out(multiplexer_1_out), .sel(H2));  // open: in1
  buf buffer_3 (buffer_1_out, H2);
  Multiplexer #(.width(2), .enable("false")) multiplexer_4 (
    .in0(2'b00), .out(multiplexer_4_out), .sel(V0));  // open: in1
  buf buffer_4 (buffer_4_out, V0);
  Multiplexer #(.width(2), .enable("false")) multiplexer_5 (
    .in0(2'b01), .out(multiplexer_4_out), .sel(V1));  // open: in1
  buf buffer_5 (buffer_4_out, V1);
  Pull_Resistor #(.pull(1)) pull_resistor_2 (.node(buffer_4_out));
  Multiplexer #(.width(2), .enable("false")) multiplexer_6 (
    .in0(2'b10), .out(multiplexer_4_out), .sel(V2));  // open: in1
  buf buffer_6 (buffer_4_out, V2);
  and and_1 (and_1_out, ~buffer_1_out, ~buffer_4_out);  // AND_Gate
  not not_1 (not_1_out, reset);
  not not_2 (not_2_out, not_3_out);
  not not_3 (not_3_out, not_4_out);
  not not_4 (not_4_out, and_1_out);
  not not_5 (not_5_out, not_6_out);
  not not_6 (not_6_out, not_7_out);
  not not_7 (not_7_out, not_1_out);
  Register #(.width(4), .trigger("high")) XY_req (
    .D({multiplexer_4_out, multiplexer_1_out}), .en(and_1_out), .Q(XY), .clk(and_1_out));  // open: clr
  and and_2 (and_2_out, and_1_out, not_2_out);
  and and_3 (and_3_out, not_1_out, not_5_out);
  S_R_Flip_Flop s_r_ff_1 (.Q(ready), .preset(and_2_out), .reset(and_3_out));  // open: S, clk, R, Qn, en

  // Notes on the sheet:
  //   ycoord
  //   coord
  //   xcoord
  //   b_press
endmodule

module Symbol_Display_Router (
  input  [1:0] SymID,
  input  clock,
  input  [3:0] XY,
  output [1:0] H0,
  output [1:0] H1,
  output [1:0] H2,
  output [1:0] V0,
  output [1:0] V1,
  output [1:0] V2
);

  wire and_1_out, and_2_out, and_3_out, and_4_out, and_5_out, and_6_out, buffer_1_out, buffer_3_out,
       buffer_4_out, buffer_5_out, buffer_6_out, pull_resistor_2_node;

  buf buffer_1 (buffer_1_out, XY[0]);
  Pull_Resistor #(.pull(1)) pull_resistor_1 (.node(buffer_1_out));
  Pull_Resistor pull_resistor_2 (.node(pull_resistor_2_node));
  buf buffer_2 (pull_resistor_2_node, XY[0]);
  buf buffer_3 (buffer_3_out, XY[0]);
  Pull_Resistor #(.pull(1)) pull_resistor_3 (.node(buffer_3_out));
  buf buffer_4 (buffer_4_out, XY[2]);
  Pull_Resistor #(.pull(1)) pull_resistor_4 (.node(buffer_4_out));
  buf buffer_5 (buffer_5_out, XY[2]);
  Pull_Resistor pull_resistor_5 (.node(buffer_5_out));
  buf buffer_6 (buffer_6_out, XY[2]);
  Pull_Resistor #(.pull(1)) pull_resistor_6 (.node(buffer_6_out));
  and and_1 (and_1_out, ~buffer_1_out, ~XY[1]);  // AND_Gate
  and and_2 (and_2_out, pull_resistor_2_node, ~XY[1]);  // AND_Gate
  and and_3 (and_3_out, ~buffer_3_out, XY[1]);  // AND_Gate
  and and_4 (and_4_out, ~buffer_4_out, ~XY[3]);  // AND_Gate
  and and_5 (and_5_out, buffer_5_out, ~XY[3]);  // AND_Gate
  and and_6 (and_6_out, ~buffer_6_out, XY[3]);  // AND_Gate
  Multiplexer #(.width(2), .enable("false")) multiplexer_1 (
    .in1({clock, SymID[0]}), .out(H0), .sel(and_1_out));  // open: in0
  Multiplexer #(.width(2), .enable("false")) multiplexer_2 (
    .in1({clock, SymID[0]}), .out(H1), .sel(and_2_out));  // open: in0
  Multiplexer #(.width(2), .enable("false")) multiplexer_3 (
    .in1({clock, SymID[0]}), .out(H2), .sel(and_3_out));  // open: in0
  Multiplexer #(.width(2), .enable("false")) multiplexer_4 (
    .in1({clock, SymID[1]}), .out(V0), .sel(and_4_out));  // open: in0
  Multiplexer #(.width(2), .enable("false")) multiplexer_5 (
    .in1({clock, SymID[1]}), .out(V1), .sel(and_5_out));  // open: in0
  Multiplexer #(.width(2), .enable("false")) multiplexer_6 (
    .in1({clock, SymID[1]}), .out(V2), .sel(and_6_out));  // open: in0

  // Other names for the same wires on the sheet: Htrue[1:0] = {clock, SymID[0]}; Vtrue[1:0] = {clock, SymID[1]}

  // Notes on the sheet:
  //   xcoord
  //   ycoord
endmodule

module Game_State_Display_Driver (
  input  [1:0] score,
  input  clock,
  output lose,
  output draw,
  output win
);

  wire [1:0] state_q;

  Register #(.width(2), .trigger("high")) state (.D(score), .en(clock), .Q(state_q), .clk(clock));  // open: clr
  and and_1 (lose, ~state_q[0], state_q[1]);  // AND_Gate
  and and_2 (draw, state_q[0], state_q[1]);
  and and_3 (win, state_q[0], ~state_q[1]);  // AND_Gate
endmodule
